# Fritzing sketch one_servo (saved by Fritzing 0.9.2b)
breadboards: 1

parts:
  Part1 = LinkIt Smart 7688 Duo
  J1 = Basic Servo

nets:
  GND: Part1.GND, J1.gnd
  5V: Part1.5V, J1.vcc
  N1: Part1.D3, J1.pulse

custom parts:
  LinkIt Smart 7688 Duo: At the heart of the platform is the MT7688AN SOC, an appliance automation bridge. This chipset is based on a powerful 802.11n 1T1R Wi-Fi AP, supports up to 2Gb RAM with additional SD-card storage, encryption engine Wi-Fi and a wide variety of peripheral connectivity options.
